# Fritzing sketch sketch (saved by Fritzing 0.9.0b)
breadboards: 1

parts:
  Part1 = Arduino Nano (Rev3.0)
  LCD_1602 = LCD screen
  Contrast_Trimmer = Trimmer Potentiometer [maximum_resistance=10kΩ package=THT]
  Hours_Knob = Trimmer Potentiometer [maximum_resistance=10kΩ package=THT]
  Minutes_Knob = Trimmer Potentiometer [maximum_resistance=10kΩ package=THT]
  Setup_Switch = SWITCH_SPDT [package=kps-1290]
  Push_Button = SWITCH-MOMENTARY-2 [package=tactile_switch_smd]
  Relay_Board = SRD-05VDC
  12V = DC Power [voltage=5]
  Solenoid_output = Solenoid

nets:
  N1: Part1.D4, Push_Button.2
  N2: Part1.D6, Setup_Switch.O
  N3: Part1.D7, LCD_1602.RS
  N4: Part1.D8, LCD_1602.E
  N5: Part1.D9, LCD_1602.DB4
  N6: Part1.D10, LCD_1602.DB5
  N7: Part1.D11/MOSI, LCD_1602.DB6
  N8: Part1.D12/MISO, LCD_1602.DB7
  N9: Part1.VIN, Relay_Board.COMMON, 12V.V+
  N10: Part1.GND, Setup_Switch.P, Push_Button.1
  VDD: Part1.5V, LCD_1602.VDD, LCD_1602.LED+, Contrast_Trimmer.leg2, Hours_Knob.leg2, Minutes_Knob.leg2, Relay_Board.VDD
  N11: Part1.A2, Minutes_Knob.wiper
  N12: Part1.A1, Hours_Knob.wiper
  N13: Part1.D13/SCK, Relay_Board.IN
  GND: LCD_1602.VSS, LCD_1602.R/W, LCD_1602.LED-, Contrast_Trimmer.leg1, Hours_Knob.leg1, Minutes_Knob.leg1, 12V.V-
  N14: LCD_1602.V0, Contrast_Trimmer.wiper
  N15: Relay_Board.NO, Solenoid_output.pin1

custom parts:
  SRD-05VDC: 5VDC Relay board for Arduino
